# Fritzing sketch 4-20mA_Pi_Hat_Design (saved by Fritzing 0.9.3b)
circuit board: 7.92945cm x 5.63654cm
breadboards: 1

parts:
  Raspberry_Pi_1 = Raspberry Pi 3 [part_number=RPI-3-V1.2]
  IC1 = ADS1015 12-bit ADC Breakout
  U1 = Voltage Regulator - 5V [package="TO220 [THT]"]
  Power_plug1 = Power plug
  R1 = Resistor [tolerance=±0.1% resistance=200 package=THT]
  LED1 = LED - 3mm [color="Red (633nm)" package="3 mm [THT]"]
  LED2 = LED - 3mm [color="Green (570nm)" package="3 mm [THT]"]
  R2 = Resistor [tolerance=±5% resistance=10k package=THT]
  R3 = Resistor [tolerance=±5% resistance=10k package=THT]

nets:
  N1: Raspberry_Pi_1.GPIO2, IC1.SDA
  N2: Raspberry_Pi_1.GPIO3, IC1.SCL
  N3: Raspberry_Pi_1.GPIO13, LED2.anode, R3.Pin_0, R3.Pin_1
  GND: Raspberry_Pi_1.GND, IC1.GND, IC1.ADDR, U1.GND, Power_plug1.GND, R1.Pin_0, LED1.cathode, LED2.cathode
  5V: Raspberry_Pi_1.5V, IC1.VDD, U1.output_voltage, LED1.anode, R2.Pin_0, R2.Pin_1
  N4: IC1.A0, R1.Pin_1
  N5: U1.input_voltage, Power_plug1.VCC

notes:
  12 VDC Power Supply
  Step Down Voltage Converter
  12 VDC --> 5 VDC
  12 VDC Supply to Current Loop
  5 VDC Supply for Raspberry Pi and ADC
  12 VDC Supply to Water Meter Current Loop
  Water Meter Current Loop
  Return
  200 ohm 0.1% Precision Shunt Resistor
  5 VDC Supply for ADC
  I2C Communication to Raspberry Pi
  10 kohm Resistors 5%
  Red LED = Power
  Green LED = Run indicator

custom parts:
  ADS1015 12-bit ADC Breakout: ADS1015 12-bit I2C ADC+PGA Breakout
