# Fritzing sketch Arduino_SD_Design (saved by Fritzing 0.9.3b)
breadboards: 1

parts:
  Part1 = Arduino Pro Mini v13
  microSD_Transflash1 = SparkFun - microSD Transflash
  R1 = Resistor [tolerance=±5% resistance=10k package=THT]
  LED1 = LED - 5mm [color="Green (565nm)" package="5 mm [THT]"]
  U1 = mystery part, 3 pins [chip_label=Hall]
  R2 = Resistor [tolerance=±5% resistance=10k package=THT]
  S1 = Pushbutton [package="[THT]"]
  C1 = Ceramic Capacitor [capacitance=100nF package="100 mil [THT, multilayer]"]
  R3 = Resistor [tolerance=±5% resistance=10k package=THT]
  U2 = mystery part, 3 pins [chip_label="3.3 V"]
  C2 = Tantalum Capacitor [capacitance=1μF package="100 mil [THT, tantalum]"]
  C3 = Tantalum Capacitor [capacitance=1μF package="100 mil [THT, tantalum]"]
  Power_plug1 = Power plug

nets:
  GND: Part1.GND, microSD_Transflash1.GND, U1.pin2, U2.pin2, C2.-, C3.-, Power_plug1.GND
  VCC: Part1.VCC, microSD_Transflash1.VCC, LED1.anode, U1.pin1, R2.Pin_1, R3.Pin_0, U2.pin3, C2.+
  N1: Part1.D13/SCK, microSD_Transflash1.SCK
  N2: Part1.D12/MISO, microSD_Transflash1.DO
  N3: Part1.D11_PWM/MOSI, microSD_Transflash1.DI
  N4: Part1.D10_PWM/SS, microSD_Transflash1.CS
  N5: Part1.D3_PWM, S1.Pin_1, S1.Pin_2, C1.1, R3.Pin_1
  N6: Part1.D2, U1.pin3, R2.Pin_0
  N7: microSD_Transflash1.CD, R1.Pin_0
  N8: R1.Pin_1, LED1.cathode
  N9: S1.Pin_3, S1.Pin_4, C1.0
  N10: U2.pin1, C3.+, Power_plug1.VCC

notes:
  To 12 V Battery
  Arduino Pro Mini
  US5881 Hall Effect Sensor (or similar)
  LED Lights when no SD card is present.
  Traco TSR 1-2433
  3.3 V Regulator
